# Fritzing sketch sketch (saved by Fritzing 0.9.3b)
circuit board: 4.24425cm x 2.35602cm
breadboards: 1

parts:
  R1 = Resistor [tolerance=±5% resistance=470 package=THT]
  R2 = Resistor [tolerance=±5% resistance=470 package=THT]
  R3 = Resistor [tolerance=±5% resistance=470 package=THT]
  Q1 = NPN-Transistor [part_number=2N2222 package="TO92 [THT]"]
  Q2 = NPN-Transistor [part_number=2N2222 package="TO92 [THT]"]
  Q3 = NPN-Transistor [part_number=2N2222 package="TO92 [THT]"]
  JP2 = Header 12 [package=1x12_machine-pin-header_lock.004]
  JP3 = M16 [package=1x16_machine-pin-header_lock.004]
  JP5 = Header 1 [package=1x01_offset]
  JP6 = Header 1 [package=1x01_offset]
  JP7 = Header 1 [package=1x01_offset]
  JP8 = Header 1 [package=1x01_offset]

nets:
  N1: R1.Pin_0, JP2.8
  N2: R1.Pin_1, Q1.B
  N3: R2.Pin_0, JP2.9
  N4: R2.Pin_1, Q2.B
  N5: R3.Pin_0, JP2.10
  N6: R3.Pin_1, Q3.B
  N7: Q1.E, Q2.E, Q3.E, JP3.4
  N8: Q1.C, JP6.1
  N9: Q2.C, JP7.1
  N10: Q3.C, JP8.1
  N11: JP2.3, JP5.1
